// Logisim project 1908028_SAP_1.circ as structural Verilog: 9 circuits, main circuit main
module main (
  input  in_1,
  input  in_2,
  input  in_3,
  input  in_4,
  input  [7:0] in_5,
  input  in_6,
  input  u_mode,
  input  o_mode,
  input  reset,
  output [3:0] out_10,
  output [7:0] out_11,
  output [7:0] out_12,
  output [7:0] out_13,
  output [7:0] out_14,
  output [7:0] out_15,
  output [7:0] out_16,
  output [7:0] out_17,
  output [7:0] out_18,
  output [7:0] out_19,
  output [7:0] out_20,
  output [7:0] out_21,
  output [7:0] out_22,
  output [7:0] out_23,
  output [7:0] out_24,
  output [7:0] out_25,
  output [7:0] out_26,
  output [7:0] out_27,
  output [7:0] out_28,
  output [3:0] out_29,
  output out_30,
  output out_31,
  output out_32,
  output out_33,
  output [7:0] out_34,
  output out_35,
  output out_36,
  output HLT
);

  wire a_in, a_out, alu_out, alu_sub, b_in, b_out, control_sequencer_1_mar_in_en, control_sequencer_1_pc_out,
       controlled_buffer_5_out, ins_reg_in_en, ins_reg_out_en, mar_in_en, Pc_en, pc_out, sram_ed;
  wire [3:0] instruction_reg_1_ins_out;

  my_program_counter my_program_counter_1 (
    .pc_en(Pc_en), .Pc_clk(in_3), .pc_reset(in_2), .pc_out_en(pc_out), .pc_out(out_29), .Pc_value(out_10));
  S_RAM s_ram_1 (
    .sram_rd(sram_ed), .sram_wr(in_1), .sram_d_in({out_34[7:4], out_29}), .mar_d_in({out_34[7:4], out_29}),
    .mar_in_en(mar_in_en), .sram_clk(in_3), .sram_d_out({out_34[7:4], out_29}), .out_8(out_12),
    .out_9(out_13), .out_10(out_14), .out_11(out_15), .out_12(out_16), .out_13(out_17), .out_14(out_18),
    .out_15(out_19), .out_16(out_21), .out_17(out_22), .out_18(out_23), .out_19(out_24), .out_20(out_25),
    .out_21(out_26), .out_22(out_27), .out_23(out_28));
  assign {out_34[7:4], out_29} = in_4 ? in_5 : 8'bz;  // Controlled_Buffer controlled_buffer_1
  my_reg my_reg_1 (
    .reg_in({out_34[7:4], out_29}), .reg_in_en(a_in), .reg_clk(in_3), .reg_out_en(a_out),
    .reg_int_out(out_11), .reg_out({out_34[7:4], out_29}));
  my_reg my_reg_2 (
    .reg_in({out_34[7:4], out_29}), .reg_in_en(b_in), .reg_clk(in_3), .reg_out_en(b_out),
    .reg_int_out(out_20), .reg_out({out_34[7:4], out_29}));
  Instruction_Reg instruction_reg_1 (
    .ins_reg_en({out_34[7:4], out_29}), .ins_reg_in_en(ins_reg_in_en), .clk(in_3),
    .ins_reg_out_en(ins_reg_out_en), .add_outs(out_29), .ins_out(instruction_reg_1_ins_out));
  control_sequencer control_sequencer_1 (
    .I7(instruction_reg_1_ins_out[3]), .I6(instruction_reg_1_ins_out[2]), .I5(instruction_reg_1_ins_out[1]),
    .I4(instruction_reg_1_ins_out[0]), .clk(controlled_buffer_5_out), .Reset(reset), .T1(out_30),
    .T2(out_31), .T3(out_32), .T4(out_33), .T5(out_35), .T6(out_36), .pc_out(control_sequencer_1_pc_out),
    .pc_en(Pc_en), .mar_in_en(control_sequencer_1_mar_in_en), .sram_rd(sram_ed),
    .ins_reg_out_en(ins_reg_out_en), .a_in(a_in), .b_in(b_in), .alu_out(alu_out), .a_out(a_out),
    .ins_reg_in_en(ins_reg_in_en), .alu_sub(alu_sub), .HLT(HLT));
  assign pc_out = o_mode ? control_sequencer_1_pc_out : 1'bz;  // Controlled_Buffer controlled_buffer_2
  my_alu my_alu_1 (
    .alu_in_1(out_11), .alu_out_en(alu_out), .alu_sub(alu_sub), .alu_in_2(out_20),
    .alu_out({out_34[7:4], out_29}));  // open: alu_carry_out
  assign mar_in_en = o_mode ? control_sequencer_1_mar_in_en : 1'bz;  // Controlled_Buffer controlled_buffer_3
  assign mar_in_en = u_mode ? in_6 : 1'bz;  // Controlled_Buffer controlled_buffer_4
  assign controlled_buffer_5_out = o_mode ? in_3 : 1'bz;  // Controlled_Buffer controlled_buffer_5

  assign out_34[3:0] = out_29;

  // Other names for the same wires on the sheet: clk = in_3; debug = in_4; debug_data[7:0] = in_5; pc_reset = in_2;
  //   sram_wr = in_1

  // Notes on the sheet:
  //   =========CODE UPLODE PART=========
endmodule

module my_alu (
  input  [7:0] alu_in_1,
  input  alu_out_en,
  input  alu_sub,
  input  [7:0] alu_in_2,
  output [7:0] alu_out,
  output alu_carry_out
);

  wire adder_2_cout, adder_3_cout, adder_4_cout, adder_5_cout, adder_6_cout, adder_7_cout, adder_8_cout,
       xor_1_out, xor_2_out, xor_3_out, xor_4_out, xor_5_out, xor_6_out, xor_7_out, xor_8_out;
  wire [7:0] adder_8_out;

  xor xor_1 (xor_1_out, alu_in_2[7], alu_sub);
  Adder #(.width(1)) adder_1 (
    .a(alu_in_1[7]), .b(xor_1_out), .out(adder_8_out[7]), .cin(adder_2_cout), .cout(alu_carry_out));
  xor xor_2 (xor_2_out, alu_in_2[6], alu_sub);
  Adder #(.width(1)) adder_2 (
    .a(alu_in_1[6]), .b(xor_2_out), .out(adder_8_out[6]), .cin(adder_3_cout), .cout(adder_2_cout));
  Adder #(.width(1)) adder_3 (
    .a(alu_in_1[5]), .b(xor_3_out), .out(adder_8_out[5]), .cin(adder_4_cout), .cout(adder_3_cout));
  xor xor_3 (xor_3_out, alu_in_2[5], alu_sub);
  xor xor_4 (xor_4_out, alu_in_2[4], alu_sub);
  Adder #(.width(1)) adder_4 (
    .a(alu_in_1[4]), .b(xor_4_out), .out(adder_8_out[4]), .cin(adder_5_cout), .cout(adder_4_cout));
  xor xor_5 (xor_5_out, alu_in_2[3], alu_sub);
  Adder #(.width(1)) adder_5 (
    .a(alu_in_1[3]), .b(xor_5_out), .out(adder_8_out[3]), .cin(adder_6_cout), .cout(adder_5_cout));
  xor xor_6 (xor_6_out, alu_in_2[2], alu_sub);
  Adder #(.width(1)) adder_6 (
    .a(alu_in_1[2]), .b(xor_6_out), .out(adder_8_out[2]), .cin(adder_7_cout), .cout(adder_6_cout));
  Adder #(.width(1)) adder_7 (
    .a(alu_in_1[1]), .b(xor_7_out), .out(adder_8_out[1]), .cin(adder_8_cout), .cout(adder_7_cout));
  xor xor_7 (xor_7_out, alu_in_2[1], alu_sub);
  xor xor_8 (xor_8_out, alu_in_2[0], alu_sub);
  Adder #(.width(1)) adder_8 (.a(alu_in_1[0]), .b(xor_8_out), .out(adder_8_out[0]), .cin(alu_sub), .cout(adder_8_cout));
  assign alu_out = alu_out_en ? adder_8_out : 8'bz;  // Controlled_Buffer controlled_buffer_1
endmodule

module my_reg (
  input  [7:0] reg_in,
  input  reg_in_en,
  input  reg_clk,
  input  reg_out_en,
  output [7:0] reg_int_out,
  output [7:0] reg_out
);

  wire multiplexer_1_out, multiplexer_2_out, multiplexer_3_out, multiplexer_4_out, multiplexer_5_out,
       multiplexer_6_out, multiplexer_7_out, multiplexer_8_out;

  Multiplexer multiplexer_1 (.in0(reg_int_out[7]), .in1(reg_in[7]), .out(multiplexer_1_out), .sel(reg_in_en));
  D_Flip_Flop d_ff_1 (.D(multiplexer_1_out), .clk(reg_clk), .Q(reg_int_out[7]));  // open: Qn, preset, reset
  Multiplexer multiplexer_2 (.in0(reg_int_out[6]), .in1(reg_in[6]), .out(multiplexer_2_out), .sel(reg_in_en));
  assign reg_out[7] = reg_out_en ? reg_int_out[7] : 1'bz;  // Controlled_Buffer controlled_buffer_1
  D_Flip_Flop d_ff_2 (.D(multiplexer_2_out), .clk(reg_clk), .Q(reg_int_out[6]));  // open: Qn, preset, reset
  Multiplexer multiplexer_3 (.in0(reg_int_out[5]), .in1(reg_in[5]), .out(multiplexer_3_out), .sel(reg_in_en));
  assign reg_out[6] = reg_out_en ? reg_int_out[6] : 1'bz;  // Controlled_Buffer controlled_buffer_2
  D_Flip_Flop d_ff_3 (.D(multiplexer_3_out), .clk(reg_clk), .Q(reg_int_out[5]));  // open: Qn, preset, reset
  Multiplexer multiplexer_4 (.in0(reg_int_out[4]), .in1(reg_in[4]), .out(multiplexer_4_out), .sel(reg_in_en));
  assign reg_out[5] = reg_out_en ? reg_int_out[5] : 1'bz;  // Controlled_Buffer controlled_buffer_3
  D_Flip_Flop d_ff_4 (.D(multiplexer_4_out), .clk(reg_clk), .Q(reg_int_out[4]));  // open: Qn, preset, reset
  Multiplexer multiplexer_5 (.in0(reg_int_out[3]), .in1(reg_in[3]), .out(multiplexer_5_out), .sel(reg_in_en));
  assign reg_out[4] = reg_out_en ? reg_int_out[4] : 1'bz;  // Controlled_Buffer controlled_buffer_4
  D_Flip_Flop d_ff_5 (.D(multiplexer_5_out), .clk(reg_clk), .Q(reg_int_out[3]));  // open: Qn, preset, reset
  assign reg_out[3] = reg_out_en ? reg_int_out[3] : 1'bz;  // Controlled_Buffer controlled_buffer_5
  Multiplexer multiplexer_6 (.in0(reg_int_out[2]), .in1(reg_in[2]), .out(multiplexer_6_out), .sel(reg_in_en));
  D_Flip_Flop d_ff_6 (.D(multiplexer_6_out), .clk(reg_clk), .Q(reg_int_out[2]));  // open: Qn, preset, reset
  Multiplexer multiplexer_7 (.in0(reg_int_out[1]), .in1(reg_in[1]), .out(multiplexer_7_out), .sel(reg_in_en));
  assign reg_out[2] = reg_out_en ? reg_int_out[2] : 1'bz;  // Controlled_Buffer controlled_buffer_6
  D_Flip_Flop d_ff_7 (.D(multiplexer_7_out), .clk(reg_clk), .Q(reg_int_out[1]));  // open: Qn, preset, reset
  Multiplexer multiplexer_8 (.in0(reg_int_out[0]), .in1(reg_in[0]), .out(multiplexer_8_out), .sel(reg_in_en));
  assign reg_out[1] = reg_out_en ? reg_int_out[1] : 1'bz;  // Controlled_Buffer controlled_buffer_7
  D_Flip_Flop d_ff_8 (.D(multiplexer_8_out), .clk(reg_clk), .Q(reg_int_out[0]));  // open: Qn, preset, reset
  assign reg_out[0] = reg_out_en ? reg_int_out[0] : 1'bz;  // Controlled_Buffer controlled_buffer_8
endmodule

module my_program_counter (
  input  pc_en,
  input  Pc_clk,
  input  pc_reset,
  input  pc_out_en,
  output [3:0] pc_out,
  output [3:0] Pc_value
);

  wire j_k_ff_2_qn, j_k_ff_3_qn, j_k_ff_4_qn;
  wire [3:0] j_k_ff_4_q;

  J_K_Flip_Flop j_k_ff_1 (
    .J(pc_en), .K(pc_en), .clk(j_k_ff_2_qn), .Q(j_k_ff_4_q[3]), .reset(pc_reset));  // open: Qn, preset
  J_K_Flip_Flop j_k_ff_2 (
    .J(pc_en), .K(pc_en), .clk(j_k_ff_3_qn), .Q(j_k_ff_4_q[2]), .Qn(j_k_ff_2_qn), .reset(pc_reset));  // open: preset
  J_K_Flip_Flop j_k_ff_3 (
    .J(pc_en), .K(pc_en), .clk(j_k_ff_4_qn), .Q(j_k_ff_4_q[1]), .Qn(j_k_ff_3_qn), .reset(pc_reset));  // open: preset
  J_K_Flip_Flop j_k_ff_4 (
    .J(pc_en), .K(pc_en), .clk(Pc_clk), .Q(j_k_ff_4_q[0]), .Qn(j_k_ff_4_qn), .reset(pc_reset));  // open: preset
  assign pc_out = pc_out_en ? j_k_ff_4_q : 4'bz;  // Controlled_Buffer controlled_buffer_1

  assign Pc_value = pc_out;
endmodule

module my_Decoder (
  input  [3:0] dec_sel,
  output [15:0] out_2
);

  wire not_1_out, not_2_out, not_3_out, not_4_out;

  not not_1 (not_1_out, dec_sel[3]);
  not not_2 (not_2_out, dec_sel[2]);
  not not_3 (not_3_out, dec_sel[1]);
  not not_4 (not_4_out, dec_sel[0]);
  and and_1 (out_2[0], not_4_out, not_3_out, not_2_out, not_1_out);
  and and_2 (out_2[1], dec_sel[0], not_3_out, not_2_out, not_1_out);
  and and_3 (out_2[2], not_4_out, dec_sel[1], not_2_out, not_1_out);
  and and_4 (out_2[3], dec_sel[0], dec_sel[1], not_2_out, not_1_out);
  and and_5 (out_2[4], not_4_out, not_3_out, dec_sel[2], not_1_out);
  and and_6 (out_2[5], dec_sel[0], not_3_out, dec_sel[2], not_1_out);
  and and_7 (out_2[6], not_4_out, dec_sel[1], dec_sel[2], not_1_out);
  and and_8 (out_2[7], dec_sel[0], dec_sel[1], dec_sel[2], not_1_out);
  and and_9 (out_2[8], not_4_out, not_3_out, not_2_out, dec_sel[3]);
  and and_10 (out_2[9], dec_sel[0], not_3_out, not_2_out, dec_sel[3]);
  and and_11 (out_2[10], not_4_out, dec_sel[1], not_2_out, dec_sel[3]);
  and and_12 (out_2[11], dec_sel[0], dec_sel[1], not_2_out, dec_sel[3]);
  and and_13 (out_2[12], not_4_out, not_3_out, dec_sel[2], dec_sel[3]);
  and and_14 (out_2[13], dec_sel[0], not_3_out, dec_sel[2], dec_sel[3]);
  and and_15 (out_2[14], not_4_out, dec_sel[1], dec_sel[2], dec_sel[3]);
  and and_16 (out_2[15], dec_sel[0], dec_sel[1], dec_sel[2], dec_sel[3]);
endmodule

module S_RAM (
  input  sram_rd,
  input  sram_wr,
  input  [7:0] sram_d_in,
  input  [7:0] mar_d_in,
  input  mar_in_en,
  input  sram_clk,
  output [7:0] sram_d_out,
  output [7:0] out_8,
  output [7:0] out_9,
  output [7:0] out_10,
  output [7:0] out_11,
  output [7:0] out_12,
  output [7:0] out_13,
  output [7:0] out_14,
  output [7:0] out_15,
  output [7:0] out_16,
  output [7:0] out_17,
  output [7:0] out_18,
  output [7:0] out_19,
  output [7:0] out_20,
  output [7:0] out_21,
  output [7:0] out_22,
  output [7:0] out_23
);

  wire [3:0] my_reg_1_reg_int_out;
  wire [7:0] controlled_buffer_1_out;
  wire [7:4] my_reg_1_reg_int_out_2;
  wire [15:0] my_decoder_1_out_2;

  my_Decoder my_decoder_1 (.dec_sel(my_reg_1_reg_int_out), .out_2(my_decoder_1_out_2));
  my_reg my_reg_1 (
    .reg_in(mar_d_in), .reg_in_en(mar_in_en), .reg_clk(sram_clk),
    .reg_int_out({my_reg_1_reg_int_out_2, my_reg_1_reg_int_out}));  // open: reg_out_en, reg_out
  assign controlled_buffer_1_out = sram_wr ? sram_d_in : 8'bz;  // Controlled_Buffer controlled_buffer_1
  Single_Ram single_ram_1 (
    .data_in(controlled_buffer_1_out), .wr_en(sram_wr), .clk(sram_clk), .cs(my_decoder_1_out_2[0]),
    .rd_en(sram_rd), .memory_content(out_8), .data_out(controlled_buffer_1_out));
  Single_Ram single_ram_2 (
    .data_in(controlled_buffer_1_out), .wr_en(sram_wr), .clk(sram_clk), .cs(my_decoder_1_out_2[1]),
    .rd_en(sram_rd), .memory_content(out_9), .data_out(controlled_buffer_1_out));
  Single_Ram single_ram_3 (
    .data_in(controlled_buffer_1_out), .wr_en(sram_wr), .clk(sram_clk), .cs(my_decoder_1_out_2[2]),
    .rd_en(sram_rd), .memory_content(out_10), .data_out(controlled_buffer_1_out));
  Single_Ram single_ram_4 (
    .data_in(controlled_buffer_1_out), .wr_en(sram_wr), .clk(sram_clk), .cs(my_decoder_1_out_2[3]),
    .rd_en(sram_rd), .memory_content(out_11), .data_out(controlled_buffer_1_out));
  Single_Ram single_ram_5 (
    .data_in(controlled_buffer_1_out), .wr_en(sram_wr), .clk(sram_clk), .cs(my_decoder_1_out_2[4]),
    .rd_en(sram_rd), .memory_content(out_12), .data_out(controlled_buffer_1_out));
  Single_Ram single_ram_6 (
    .data_in(controlled_buffer_1_out), .wr_en(sram_wr), .clk(sram_clk), .cs(my_decoder_1_out_2[5]),
    .rd_en(sram_rd), .memory_content(out_13), .data_out(controlled_buffer_1_out));
  Single_Ram single_ram_7 (
    .data_in(controlled_buffer_1_out), .wr_en(sram_wr), .clk(sram_clk), .cs(my_decoder_1_out_2[6]),
    .rd_en(sram_rd), .memory_content(out_14), .data_out(controlled_buffer_1_out));
  Single_Ram single_ram_8 (
    .data_in(controlled_buffer_1_out), .wr_en(sram_wr), .clk(sram_clk), .cs(my_decoder_1_out_2[7]),
    .rd_en(sram_rd), .memory_content(out_15), .data_out(controlled_buffer_1_out));
  Single_Ram single_ram_9 (
    .data_in(controlled_buffer_1_out), .wr_en(sram_wr), .clk(sram_clk), .cs(my_decoder_1_out_2[8]),
    .rd_en(sram_rd), .memory_content(out_16), .data_out(controlled_buffer_1_out));
  Single_Ram single_ram_10 (
    .data_in(controlled_buffer_1_out), .wr_en(sram_wr), .clk(sram_clk), .cs(my_decoder_1_out_2[9]),
    .rd_en(sram_rd), .memory_content(out_17), .data_out(controlled_buffer_1_out));
  Single_Ram single_ram_11 (
    .data_in(controlled_buffer_1_out), .wr_en(sram_wr), .clk(sram_clk), .cs(my_decoder_1_out_2[10]),
    .rd_en(sram_rd), .memory_content(out_18), .data_out(controlled_buffer_1_out));
  Single_Ram single_ram_12 (
    .data_in(controlled_buffer_1_out), .wr_en(sram_wr), .clk(sram_clk), .cs(my_decoder_1_out_2[11]),
    .rd_en(sram_rd), .memory_content(out_19), .data_out(controlled_buffer_1_out));
  Single_Ram single_ram_13 (
    .data_in(controlled_buffer_1_out), .wr_en(sram_wr), .clk(sram_clk), .cs(my_decoder_1_out_2[12]),
    .rd_en(sram_rd), .memory_content(out_20), .data_out(controlled_buffer_1_out));
  Single_Ram single_ram_14 (
    .data_in(controlled_buffer_1_out), .wr_en(sram_wr), .clk(sram_clk), .cs(my_decoder_1_out_2[13]),
    .rd_en(sram_rd), .memory_content(out_21), .data_out(controlled_buffer_1_out));
  Single_Ram single_ram_15 (
    .data_in(controlled_buffer_1_out), .wr_en(sram_wr), .clk(sram_clk), .cs(my_decoder_1_out_2[14]),
    .rd_en(sram_rd), .memory_content(out_22), .data_out(controlled_buffer_1_out));
  Single_Ram single_ram_16 (
    .data_in(controlled_buffer_1_out), .wr_en(sram_wr), .clk(sram_clk), .cs(my_decoder_1_out_2[15]),
    .rd_en(sram_rd), .memory_content(out_23), .data_out(controlled_buffer_1_out));
  assign sram_d_out = sram_rd ? controlled_buffer_1_out : 8'bz;  // Controlled_Buffer controlled_buffer_2
endmodule

module Single_Ram (
  input  [7:0] data_in,
  input  wr_en,
  input  clk,
  input  cs,
  input  rd_en,
  output [7:0] memory_content,
  output [7:0] data_out
);

  wire and_1_out, and_2_out;

  and and_1 (and_1_out, wr_en, cs);
  and and_2 (and_2_out, cs, rd_en);
  my_reg my_reg_1 (
    .reg_in(data_in), .reg_in_en(and_1_out), .reg_clk(clk), .reg_out_en(and_2_out),
    .reg_int_out(memory_content), .reg_out(data_out));
endmodule

module Instruction_Reg (
  input  [7:0] ins_reg_en,
  input  ins_reg_in_en,
  input  clk,
  input  ins_reg_out_en,
  output [3:0] add_outs,
  output [3:0] ins_out
);

  wire [3:0] my_reg_1_reg_int_out;

  my_reg my_reg_1 (
    .reg_in(ins_reg_en), .reg_in_en(ins_reg_in_en), .reg_clk(clk),
    .reg_int_out({ins_out, my_reg_1_reg_int_out}));  // open: reg_out_en, reg_out
  assign add_outs = ins_reg_out_en ? my_reg_1_reg_int_out : 4'bz;  // Controlled_Buffer controlled_buffer_1
endmodule

module control_sequencer (
  input  I7,
  input  I6,
  input  I5,
  input  I4,
  input  clk,
  input  Reset,
  output T1,
  output T2,
  output T3,
  output T4,
  output T5,
  output T6,
  output pc_out,
  output pc_en,
  output mar_in_en,
  output sram_rd,
  output ins_reg_out_en,
  output a_in,
  output b_in,
  output alu_out,
  output a_out,
  output ins_reg_in_en,
  output alu_sub,
  output HLT
);

  wire and_1_out, and_2_out, and_3_out, and_4_out, and_6_out, and_7_out, and_8_out, and_9_out, and_10_out,
       and_11_out, and_12_out, and_13_out, and_14_out, and_15_out, and_16_out, j_k_ff_1_q, j_k_ff_2_qn,
       j_k_ff_3_qn, j_k_ff_4_qn, j_k_ff_5_qn, j_k_ff_6_qn, not_1_out, not_2_out, not_3_out, not_4_out,
       or_2_out, or_3_out, or_6_out, or_8_out, or_9_out;

  not not_1 (not_1_out, I7);
  not not_2 (not_2_out, I6);
  not not_3 (not_3_out, I5);
  not not_4 (not_4_out, I4);
  and and_1 (and_1_out, I4, I5, not_2_out, not_1_out);
  and and_2 (and_2_out, I4, not_3_out, not_2_out, not_1_out);
  and and_3 (and_3_out, not_4_out, I5, not_2_out, not_1_out);
  and and_4 (and_4_out, not_4_out, I5, I6, I7);
  and and_5 (HLT, I4, I5, I6, I7);
  J_K_Flip_Flop j_k_ff_1 (
    .J(j_k_ff_6_qn), .K(T6), .clk(clk), .Q(j_k_ff_1_q), .Qn(pc_out), .reset(Reset));  // open: preset
  J_K_Flip_Flop j_k_ff_2 (
    .J(pc_out), .K(j_k_ff_1_q), .clk(clk), .Q(ins_reg_in_en), .Qn(j_k_ff_2_qn), .reset(Reset));  // open: preset
  and and_6 (and_6_out, T4, and_2_out);
  and and_7 (and_7_out, T4, or_2_out);
  or or_1 (mar_in_en, pc_out, and_6_out, and_7_out, and_8_out);
  J_K_Flip_Flop j_k_ff_3 (
    .J(ins_reg_in_en), .K(j_k_ff_2_qn), .clk(clk), .Q(pc_en), .Qn(j_k_ff_3_qn), .reset(Reset));  // open: preset
  or or_2 (or_2_out, and_1_out, and_3_out);
  and and_8 (and_8_out, T4, and_4_out);
  and and_9 (and_9_out, T5, and_2_out);
  J_K_Flip_Flop j_k_ff_4 (
    .J(pc_en), .K(j_k_ff_3_qn), .clk(clk), .Q(T4), .Qn(j_k_ff_4_qn), .reset(Reset));  // open: preset
  or or_3 (or_3_out, and_1_out, and_3_out);
  and and_10 (and_10_out, T5, or_3_out);
  and and_11 (and_11_out, T5, and_4_out);
  or or_4 (sram_rd, ins_reg_in_en, and_9_out, and_10_out, and_11_out);
  J_K_Flip_Flop j_k_ff_5 (.J(T4), .K(j_k_ff_4_qn), .clk(clk), .Q(T5), .Qn(j_k_ff_5_qn), .reset(Reset));  // open: preset
  and and_12 (and_12_out, T4, and_1_out);
  J_K_Flip_Flop j_k_ff_6 (.J(T5), .K(j_k_ff_5_qn), .clk(clk), .Q(T6), .Qn(j_k_ff_6_qn), .reset(Reset));  // open: preset
  and and_13 (and_13_out, T4, and_3_out);
  and and_14 (and_14_out, T4, and_2_out);
  or or_5 (ins_reg_out_en, and_12_out, and_14_out, and_13_out);
  and and_15 (and_15_out, T5, and_2_out);
  or or_6 (or_6_out, and_3_out, and_1_out);
  and and_16 (and_16_out, T6, or_6_out);
  or or_7 (a_in, and_15_out, and_16_out);
  or or_8 (or_8_out, and_1_out, and_3_out);
  and and_17 (b_in, T5, or_8_out);
  or or_9 (or_9_out, and_1_out, and_3_out);
  and and_18 (alu_out, T6, or_9_out);
  and and_19 (a_out, T4, and_4_out);
  and and_20 (alu_sub, T6, and_1_out);

  assign T1 = pc_out;
  assign T2 = ins_reg_in_en;
  assign T3 = pc_en;

  // Notes on the sheet:
  //   SUB
  //   LDA
  //   ADD
  //   OUT
endmodule
